// Digital circuit P05 (2).dig as structural Verilog
module P05__2 (
  input  [7:0] a,
  input  [2:0] sh,
  output [7:0] y
);

  wire [7:0] multiplexer_1_out, multiplexer_2_out;

  Multiplexer #(.Bits(8)) multiplexer_1 (.sel(sh[0]), .in_0(a), .in_1({a[6:0], 1'b0}), .out(multiplexer_1_out));
  Multiplexer #(.Bits(8)) multiplexer_2 (
    .sel(sh[1]), .in_0(multiplexer_1_out), .in_1({multiplexer_1_out[5:0], 2'b00}), .out(multiplexer_2_out));
  Multiplexer #(.Bits(8)) multiplexer_3 (
    .sel(sh[2]), .in_0(multiplexer_2_out), .in_1({multiplexer_2_out[3:0], 4'b0000}), .out(y));
endmodule

/* Test case public tests:
a sh y
23 0 23
9 0 9
0 4 0
152 6 0
240 6 0
172 6 0
0 4 0
54 2 216
10 0 10
67 4 48
82 7 0
139 7 128
0 0 0
128 5 0
9 3 72
34 0 34
0 2 0
127 3 248
127 0 127
110 2 184
183 5 224
255 3 248
49 4 16
75 6 192
1 3 8
179 2 204
128 0 128
3 3 24
128 3 0
35 2 140
208 7 0
145 2 68
11 6 192
21 4 80
255 3 248
81 3 136
3 3 24
6 0 6
0 0 0
30 7 0
19 0 19
255 7 128
198 5 192
127 0 127
214 3 176
255 5 224
72 3 64
92 6 0
123 5 96
244 1 232
194 7 0
64 2 0
128 3 0
154 7 0
127 3 248
67 5 96
127 2 252
128 5 0
176 7 0
195 2 12
128 1 0
3 7 128
255 3 248
255 7 128
64 4 0
167 3 56
118 0 118
120 7 0
93 0 93
13 5 160
230 3 48
84 0 84
127 1 254
4 2 16
211 0 211
255 5 224
128 2 0
255 3 248
128 0 128
31 0 31
151 7 128
81 4 16
239 1 222
112 6 0
24 5 0
226 1 196
0 7 0
239 0 239
7 5 224
21 6 64
29 4 208
6 0 6
115 3 152
26 6 128
123 5 96
166 2 152
115 4 48
15 0 15
11 6 192
102 3 48
8 7 0
29 5 160
15 3 120
128 0 128
127 4 240
25 2 100
170 2 168
0 2 0
15 1 30
0 4 0
221 0 221
9 4 144
11 6 192
242 4 32
25 1 50
95 3 248
26 5 64
153 7 128
51 7 128
117 2 212
7 4 112
250 1 244
19 3 152
215 3 184
25 7 128
68 5 128
135 3 56
190 6 128
117 5 160
124 3 224
117 4 80
152 6 0
177 1 98
0 6 0
0 6 0
121 5 32
0 6 0
255 3 248
79 0 79
192 4 0
0 4 0
77 0 77
10 7 0
0 7 0
255 7 128
105 5 32
45 1 90
21 5 160
52 3 160
95 7 128
44 0 44
24 7 0
246 5 192
200 6 0
147 3 152
6 2 24
114 5 64
3 4 48
128 7 0
8 5 0
*/
