// Digital circuit P07.dig as structural Verilog
module P07 (
  input  [3:0] a,
  input  [3:0] b,
  output lt,
  output ltu
);

  wire and_2_out, and_3_out, and_4_out, and_5_out, and_6_out, and_7_out, and_8_out, and_9_out, c0, c1, c2,
       not_1_out, not_2_out, not_3_out, not_4_out, not_5_out, not_6_out, not_7_out, not_8_out, not_9_out,
       xor_1_out, xor_2_out, xor_3_out, xor_4_out;

  not not_1 (not_1_out, a[0]);
  and and_1 (c0, not_1_out, b[0]);
  not not_2 (not_2_out, a[1]);
  and and_2 (and_2_out, not_2_out, b[1]);
  xor xor_1 (xor_1_out, a[1], b[1]);
  not not_3 (not_3_out, a[2]);
  and and_3 (and_3_out, not_3_out, b[2]);
  xor xor_2 (xor_2_out, a[2], b[2]);
  not not_4 (not_4_out, a[3]);
  and and_4 (and_4_out, not_4_out, b[3]);
  xor xor_3 (xor_3_out, a[3], b[3]);
  not not_5 (not_5_out, xor_1_out);
  not not_6 (not_6_out, xor_2_out);
  not not_7 (not_7_out, xor_3_out);
  and and_5 (and_5_out, not_5_out, c0);
  and and_6 (and_6_out, not_6_out, c1);
  and and_7 (and_7_out, not_7_out, c2);
  or or_1 (c1, and_2_out, and_5_out);
  or or_2 (c2, and_3_out, and_6_out);
  or or_3 (ltu, and_4_out, and_7_out);
  and and_8 (and_8_out, a[3], not_8_out);
  not not_8 (not_8_out, b[3]);
  xor xor_4 (xor_4_out, a[3], b[3]);
  not not_9 (not_9_out, xor_4_out);
  and and_9 (and_9_out, not_9_out, ltu);
  or or_4 (lt, and_8_out, and_9_out);

  // Other names for the same wires on the sheet: ltu_net = ltu

  // Notes on the sheet:
  //   P07 Less-than unit (signed and unsigned) - Digital task
  //   4-bit version from gates: design a 1-bit comparator cell with a K-map, cascade it, then fix the sign bit for the signed result.
  //   Allowed parts: And, Or, Not, NAnd, NOr, XOr, XNOr + wiring parts
  //   Do not rename, move or delete the input and output pins.
endmodule

/* Test case public tests:
a b lt ltu
0 0 0 0
0 1 1 1
0 2 1 1
0 3 1 1
0 4 1 1
0 5 1 1
0 6 1 1
0 7 1 1
0 8 0 1
0 9 0 1
0 10 0 1
0 11 0 1
0 12 0 1
0 13 0 1
0 14 0 1
0 15 0 1
1 0 0 0
1 1 0 0
1 2 1 1
1 3 1 1
1 4 1 1
1 5 1 1
1 6 1 1
1 7 1 1
1 8 0 1
1 9 0 1
1 10 0 1
1 11 0 1
1 12 0 1
1 13 0 1
1 14 0 1
1 15 0 1
2 0 0 0
2 1 0 0
2 2 0 0
2 3 1 1
2 4 1 1
2 5 1 1
2 6 1 1
2 7 1 1
2 8 0 1
2 9 0 1
2 10 0 1
2 11 0 1
2 12 0 1
2 13 0 1
2 14 0 1
2 15 0 1
3 0 0 0
3 1 0 0
3 2 0 0
3 3 0 0
3 4 1 1
3 5 1 1
3 6 1 1
3 7 1 1
3 8 0 1
3 9 0 1
3 10 0 1
3 11 0 1
3 12 0 1
3 13 0 1
3 14 0 1
3 15 0 1
4 0 0 0
4 1 0 0
4 2 0 0
4 3 0 0
4 4 0 0
4 5 1 1
4 6 1 1
4 7 1 1
4 8 0 1
4 9 0 1
4 10 0 1
4 11 0 1
4 12 0 1
4 13 0 1
4 14 0 1
4 15 0 1
5 0 0 0
5 1 0 0
5 2 0 0
5 3 0 0
5 4 0 0
5 5 0 0
5 6 1 1
5 7 1 1
5 8 0 1
5 9 0 1
5 10 0 1
5 11 0 1
5 12 0 1
5 13 0 1
5 14 0 1
5 15 0 1
6 0 0 0
6 1 0 0
6 2 0 0
6 3 0 0
6 4 0 0
6 5 0 0
6 6 0 0
6 7 1 1
6 8 0 1
6 9 0 1
6 10 0 1
6 11 0 1
6 12 0 1
6 13 0 1
6 14 0 1
6 15 0 1
7 0 0 0
7 1 0 0
7 2 0 0
7 3 0 0
7 4 0 0
7 5 0 0
7 6 0 0
7 7 0 0
7 8 0 1
7 9 0 1
7 10 0 1
7 11 0 1
7 12 0 1
7 13 0 1
7 14 0 1
7 15 0 1
8 0 1 0
8 1 1 0
8 2 1 0
8 3 1 0
8 4 1 0
8 5 1 0
8 6 1 0
8 7 1 0
8 8 0 0
8 9 1 1
8 10 1 1
8 11 1 1
8 12 1 1
8 13 1 1
8 14 1 1
8 15 1 1
9 0 1 0
9 1 1 0
9 2 1 0
9 3 1 0
9 4 1 0
9 5 1 0
9 6 1 0
9 7 1 0
9 8 0 0
9 9 0 0
9 10 1 1
9 11 1 1
9 12 1 1
9 13 1 1
9 14 1 1
9 15 1 1
10 0 1 0
10 1 1 0
10 2 1 0
10 3 1 0
10 4 1 0
10 5 1 0
10 6 1 0
10 7 1 0
10 8 0 0
10 9 0 0
10 10 0 0
10 11 1 1
10 12 1 1
10 13 1 1
10 14 1 1
10 15 1 1
11 0 1 0
11 1 1 0
11 2 1 0
11 3 1 0
11 4 1 0
11 5 1 0
11 6 1 0
11 7 1 0
11 8 0 0
11 9 0 0
11 10 0 0
11 11 0 0
11 12 1 1
11 13 1 1
11 14 1 1
11 15 1 1
12 0 1 0
12 1 1 0
12 2 1 0
12 3 1 0
12 4 1 0
12 5 1 0
12 6 1 0
12 7 1 0
12 8 0 0
12 9 0 0
12 10 0 0
12 11 0 0
12 12 0 0
12 13 1 1
12 14 1 1
12 15 1 1
13 0 1 0
13 1 1 0
13 2 1 0
13 3 1 0
13 4 1 0
13 5 1 0
13 6 1 0
13 7 1 0
13 8 0 0
13 9 0 0
13 10 0 0
13 11 0 0
13 12 0 0
13 13 0 0
13 14 1 1
13 15 1 1
14 0 1 0
14 1 1 0
14 2 1 0
14 3 1 0
14 4 1 0
14 5 1 0
14 6 1 0
14 7 1 0
14 8 0 0
14 9 0 0
14 10 0 0
14 11 0 0
14 12 0 0
14 13 0 0
14 14 0 0
14 15 1 1
15 0 1 0
15 1 1 0
15 2 1 0
15 3 1 0
15 4 1 0
15 5 1 0
15 6 1 0
15 7 1 0
15 8 0 0
15 9 0 0
15 10 0 0
15 11 0 0
15 12 0 0
15 13 0 0
15 14 0 0
15 15 0 0
*/
