// Digital circuit P11.dig as structural Verilog
module P11 (
  input  we,
  input  [4:0] rd,
  output [31:0] wen
);

  wire hi0, hi1, hi2, hi3, lo0, lo1, lo2, lo3, lo4, lo5, lo6, lo7, r0n, r1n, r2n, r3n, r4n;

  not not_1 (r0n, rd[0]);
  not not_2 (r1n, rd[1]);
  not not_3 (r2n, rd[2]);
  not not_4 (r3n, rd[3]);
  not not_5 (r4n, rd[4]);
  and and_1 (lo0, r0n, r1n, r2n);
  and and_2 (lo1, rd[0], r1n, r2n);
  and and_3 (lo2, r0n, rd[1], r2n);
  and and_4 (lo3, rd[0], rd[1], r2n);
  and and_5 (lo4, r0n, r1n, rd[2]);
  and and_6 (lo5, rd[0], r1n, rd[2]);
  and and_7 (lo6, r0n, rd[1], rd[2]);
  and and_8 (lo7, rd[0], rd[1], rd[2]);
  and and_9 (hi0, we, r3n, r4n);
  and and_10 (hi1, we, rd[3], r4n);
  and and_11 (hi2, we, r3n, rd[4]);
  and and_12 (hi3, we, rd[3], rd[4]);
  and and_13 (wen[1], hi0, lo1);
  and and_14 (wen[2], hi0, lo2);
  and and_15 (wen[3], hi0, lo3);
  and and_16 (wen[4], hi0, lo4);
  and and_17 (wen[5], hi0, lo5);
  and and_18 (wen[6], hi0, lo6);
  and and_19 (wen[7], hi0, lo7);
  and and_20 (wen[8], hi1, lo0);
  and and_21 (wen[9], hi1, lo1);
  and and_22 (wen[10], hi1, lo2);
  and and_23 (wen[11], hi1, lo3);
  and and_24 (wen[12], hi1, lo4);
  and and_25 (wen[13], hi1, lo5);
  and and_26 (wen[14], hi1, lo6);
  and and_27 (wen[15], hi1, lo7);
  and and_28 (wen[16], hi2, lo0);
  and and_29 (wen[17], hi2, lo1);
  and and_30 (wen[18], hi2, lo2);
  and and_31 (wen[19], hi2, lo3);
  and and_32 (wen[20], hi2, lo4);
  and and_33 (wen[21], hi2, lo5);
  and and_34 (wen[22], hi2, lo6);
  and and_35 (wen[23], hi2, lo7);
  and and_36 (wen[24], hi3, lo0);
  and and_37 (wen[25], hi3, lo1);
  and and_38 (wen[26], hi3, lo2);
  and and_39 (wen[27], hi3, lo3);
  and and_40 (wen[28], hi3, lo4);
  and and_41 (wen[29], hi3, lo5);
  and and_42 (wen[30], hi3, lo6);
  and and_43 (wen[31], hi3, lo7);

  assign wen[0] = 1'b0;

  // Other names for the same wires on the sheet: r0 = rd[0]; r1 = rd[1]; r2 = rd[2]; r3 = rd[3]; r4 = rd[4];
  //   w1 = wen[1]; w2 = wen[2]; w3 = wen[3]; w4 = wen[4]; w5 = wen[5]; w6 = wen[6]; w7 = wen[7]; w8 = wen[8];
  //   w9 = wen[9]; w10 = wen[10]; w11 = wen[11]; w12 = wen[12]; w13 = wen[13]; w14 = wen[14]; w15 = wen[15];
  //   w16 = wen[16]; w17 = wen[17]; w18 = wen[18]; w19 = wen[19]; w20 = wen[20]; w21 = wen[21]; w22 = wen[22];
  //   w23 = wen[23]; w24 = wen[24]; w25 = wen[25]; w26 = wen[26]; w27 = wen[27]; w28 = wen[28]; w29 = wen[29];
  //   w30 = wen[30]; w31 = wen[31]

  // Notes on the sheet:
  //   P11 Register-file write decoder - Digital task
endmodule
