// Digital circuit P20.dig as structural Verilog
module P20 (
  input  [2:0] immsel,
  input  [3:0] imm_i,
  input  [3:0] imm_s,
  input  [3:0] imm_b,
  input  [3:0] imm_u,
  input  [3:0] imm_j,
  output [3:0] imm
);

  Multiplexer #(.Bits(4), .Selector_Bits(3)) multiplexer_1 (
    .sel(immsel), .in_0(imm_i), .in_1(imm_s), .in_2(imm_b), .in_3(imm_u), .in_4(imm_j), .in_5(4'b0000),
    .in_6(4'b0000), .in_7(4'b0000), .out(imm));

  // Notes on the sheet:
  //   P20 Immediate selector - Digital task
  //   4-bit version with a multiplexer.
  //   Allowed parts: gates + Multiplexer, Demultiplexer, Decoder, PriorityEncoder
  //   Do not rename, move or delete the input and output pins.
endmodule

/* Test case public tests:
immsel imm_i imm_s imm_b imm_u imm_j imm
3 8 1 11 9 11 9
0 14 6 9 8 7 14
5 7 15 13 15 5 0
4 4 0 14 2 0 0
2 0 8 10 7 0 10
1 15 6 0 9 0 6
5 0 2 8 8 14 0
0 8 0 8 9 0 8
3 13 10 10 5 13 5
3 7 13 8 3 9 3
3 14 1 4 6 14 6
4 4 1 15 9 0 0
5 7 7 11 4 14 0
2 0 14 15 0 0 15
0 5 12 10 3 6 5
3 4 8 0 1 4 1
1 7 15 15 13 4 15
5 0 7 1 7 12 0
2 13 13 6 0 11 6
4 0 15 15 9 0 0
4 12 1 1 0 5 5
4 1 6 8 2 5 5
1 14 1 13 4 4 1
4 2 0 8 13 9 9
4 11 11 7 13 0 0
4 8 11 6 8 5 5
5 13 4 2 7 8 0
1 15 6 0 11 8 6
1 1 0 14 8 10 0
0 9 5 5 4 2 9
2 9 2 0 10 0 0
0 14 13 4 14 15 14
3 1 15 11 6 6 6
1 5 15 12 9 7 15
5 10 3 1 8 12 0
5 7 3 8 14 6 0
2 0 15 0 8 9 0
1 8 9 11 7 0 9
3 9 12 13 7 0 7
0 15 0 5 6 4 15
4 2 12 1 8 8 8
5 14 6 9 2 14 0
3 3 0 14 1 13 1
5 5 15 7 10 1 0
5 12 6 0 8 0 0
0 11 7 10 12 15 11
2 0 0 2 15 3 2
1 4 0 7 1 4 0
3 7 7 8 15 9 15
4 0 4 3 3 7 7
2 3 8 4 8 4 4
5 4 14 3 8 15 0
3 9 3 15 7 5 7
1 3 14 13 0 3 14
4 12 0 0 0 11 11
3 9 8 6 0 10 0
0 14 15 5 0 15 14
4 5 5 8 6 14 14
0 5 7 0 10 8 5
2 7 8 1 14 2 1
4 0 8 14 9 5 5
5 4 11 11 2 3 0
4 15 0 13 15 0 0
5 0 0 4 14 14 0
4 11 1 2 13 6 6
1 14 8 10 1 9 8
1 0 2 3 10 12 2
3 7 15 7 15 4 15
1 10 13 5 6 11 13
4 3 15 11 8 15 15
3 8 9 8 5 0 5
1 8 12 14 15 15 12
1 14 8 2 3 8 8
3 12 14 3 14 2 14
1 7 7 2 4 15 7
3 0 14 2 15 7 15
3 10 9 10 7 7 7
1 6 10 1 2 12 10
0 0 7 3 14 8 0
4 7 12 6 12 6 6
3 0 8 8 3 3 3
3 9 0 8 15 7 15
3 12 6 12 14 13 14
4 4 0 2 11 8 8
5 1 8 0 6 9 0
5 0 3 4 15 6 0
5 14 1 1 8 12 0
2 7 9 13 11 8 13
2 8 8 0 0 8 0
2 0 5 11 5 15 11
3 13 15 15 7 2 7
2 8 6 15 7 0 15
4 9 0 4 2 7 7
2 2 7 2 1 7 2
2 6 0 10 2 4 10
0 11 4 1 6 0 11
3 15 5 14 8 10 8
0 10 12 0 15 7 10
1 1 7 13 14 15 7
4 14 7 0 15 9 9
5 6 8 0 2 6 0
5 8 9 3 2 4 0
4 0 7 3 8 10 10
3 15 0 10 0 15 0
5 10 14 15 15 6 0
2 0 15 3 0 15 3
5 15 3 10 4 12 0
2 0 11 3 15 4 3
4 3 6 9 2 12 12
5 0 11 8 7 0 0
4 14 15 8 4 8 8
5 0 2 0 3 8 0
3 9 0 8 1 3 1
5 0 5 11 0 15 0
5 3 12 4 4 4 0
0 10 8 1 8 15 10
3 4 8 4 10 15 10
3 15 2 10 0 5 0
1 0 0 15 3 8 0
5 5 10 3 4 3 0
0 2 0 6 6 14 2
0 4 10 14 0 8 4
4 5 6 10 2 7 7
3 4 9 8 7 2 7
1 10 11 8 12 1 11
0 1 12 6 15 7 1
2 9 15 1 0 14 1
4 15 9 7 7 8 8
0 8 15 9 8 8 8
5 10 2 15 9 1 0
0 0 8 8 5 10 0
0 0 9 0 9 4 0
5 6 15 2 15 8 0
3 8 7 2 14 4 14
3 7 6 13 8 15 8
3 7 6 14 1 14 1
0 12 5 14 4 9 12
5 8 8 11 8 13 0
4 7 5 4 8 7 7
5 0 8 8 0 15 0
5 6 15 12 10 8 0
3 8 15 14 10 11 10
5 3 0 11 0 3 0
1 5 11 5 15 11 11
0 10 15 6 1 0 10
1 12 9 10 12 7 9
1 15 0 3 1 13 0
5 2 3 10 0 7 0
1 8 3 9 4 15 3
3 3 15 2 0 8 0
1 10 8 6 6 7 8
2 8 7 0 13 8 0
3 0 15 9 8 0 8
0 14 8 15 0 4 14
4 6 0 0 8 1 1
5 10 2 10 12 0 0
5 8 14 10 6 14 0
4 15 2 1 7 14 14
1 0 15 15 14 7 15
4 11 14 15 3 1 1
*/
