// Digital circuit P21.dig as structural Verilog
module P21 (
  input  [31:0] instr,
  output is_lui,
  output is_auipc,
  output is_jal,
  output is_jalr,
  output is_branch,
  output is_load,
  output is_store,
  output is_opimm,
  output is_op,
  output is_system,
  output is_ecall,
  output is_mret
);

  and and_1 (is_lui, instr[0], instr[1], instr[2], ~instr[3], instr[4], instr[5], ~instr[6]);  // And
  and and_2 (is_auipc, instr[0], instr[1], instr[2], ~instr[3], instr[4], ~instr[5], ~instr[6]);  // And
  and and_3 (is_jal, instr[0], instr[1], instr[2], instr[3], ~instr[4], instr[5], instr[6]);  // And
  and and_4 (is_jalr, instr[0], instr[1], instr[2], ~instr[3], ~instr[4], instr[5], instr[6]);  // And
  and and_5 (is_branch, instr[0], instr[1], ~instr[2], ~instr[3], ~instr[4], instr[5], instr[6]);  // And
  and and_6 (is_load, instr[0], instr[1], ~instr[2], ~instr[3], ~instr[4], ~instr[5], ~instr[6]);  // And
  and and_7 (is_store, instr[0], instr[1], ~instr[2], ~instr[3], ~instr[4], instr[5], ~instr[6]);  // And
  and and_8 (is_opimm, instr[0], instr[1], ~instr[2], ~instr[3], instr[4], ~instr[5], ~instr[6]);  // And
  and and_9 (is_op, instr[0], instr[1], ~instr[2], ~instr[3], instr[4], instr[5], ~instr[6]);  // And
  and and_10 (is_system, instr[0], instr[1], ~instr[2], ~instr[3], instr[4], instr[5], instr[6]);  // And
  Comparator #(.Bits(32)) comparator_1 (.a(instr), .b(32'h73), .eq(is_ecall));  // open: gt, lt
  Comparator #(.Bits(32)) comparator_2 (.a(instr), .b(32'h30200073), .eq(is_mret));  // open: gt, lt

  // Notes on the sheet:
  //   P21 Opcode class decoder - Digital task
  //   Full size: AND gates with inverted inputs for each opcode; a Comparator with a Const is allowed for ECALL/MRET.
  //   Allowed parts: all of the above + Add, Sub, Comparator, Neg
  //   Do not rename, move or delete the input and output pins.
  //   Splitter: low 7 bits of instr = opcode bits 0..6
  //   opcode bit:
  //   4
  //   5
  //   6
  //   0
  //   1
  //   2
  //   3
  //   AND gates (7 inputs): ring = inverted input, i.e. opcode bit must be 0
  //   LUI  0110111
  //   AUIPC  0010111
  //   JAL  1101111
  //   JALR  1100111
  //   BRANCH  1100011
  //   LOAD  0000011
  //   STORE  0100011
  //   OP-IMM  0010011
  //   OP  0110011
  //   SYSTEM  1110011
  //   is_ecall = (instr == 0x00000073)
  //   is_mret = (instr == 0x30200073)
endmodule

/* Test case public tests:
instr is_lui is_auipc is_jal is_jalr is_branch is_load is_store is_opimm is_op is_system is_ecall is_mret
115 0 0 0 0 0 0 0 0 0 1 1 0
15132211 0 0 0 0 0 0 0 0 1 0 0 0
5452435 0 0 0 0 0 0 0 1 0 0 0 0
3478803 0 0 0 0 0 0 0 1 0 0 0 0
12656771 0 0 0 0 0 1 0 0 0 0 0 0
4358375 0 0 0 1 0 0 0 0 0 0 0 0
4358375 0 0 0 1 0 0 0 0 0 0 0 0
18380723 0 0 0 0 0 0 0 0 1 0 0 0
273678451 0 0 0 0 0 0 0 0 0 1 0 0
32431667 0 0 0 0 0 0 0 0 1 0 0 0
1048691 0 0 0 0 0 0 0 0 0 1 0 0
1073750067 0 0 0 0 0 0 0 0 1 0 0 0
3058015673 0 0 0 0 0 0 0 0 0 0 0 0
1081497107 0 0 0 0 0 0 0 1 0 0 0 0
32888211 0 0 0 0 0 0 0 1 0 0 0 0
5452435 0 0 0 0 0 0 0 1 0 0 0 0
305419575 1 0 0 0 0 0 0 0 0 0 0 0
20483 0 0 0 0 0 1 0 0 0 0 0 0
133588371 0 0 0 0 0 0 0 1 0 0 0 0
22686131 0 0 0 0 0 0 0 0 1 0 0 0
12323 0 0 0 0 0 0 1 0 0 0 0 0
4294967295 0 0 0 0 0 0 0 0 0 0 0 0
19174451 0 0 0 0 0 0 0 0 1 0 0 0
4246240483 0 0 0 0 1 0 0 0 0 0 0 0
1073750067 0 0 0 0 0 0 0 0 1 0 0 0
15 0 0 0 0 0 0 0 0 0 0 0 0
20483 0 0 0 0 0 1 0 0 0 0 0 0
3212547 0 0 0 0 0 1 0 0 0 0 0 0
5452435 0 0 0 0 0 0 0 1 0 0 0 0
19 0 0 0 0 0 0 0 1 0 0 0 0
4207 0 0 1 0 0 0 0 0 0 0 0 0
3478803 0 0 0 0 0 0 0 1 0 0 0 0
810750707 0 0 0 0 0 0 0 0 0 1 0 0
4887 0 1 0 0 0 0 0 0 0 0 0 0
1708998647 0 0 0 0 0 0 0 0 0 0 0 0
4277626595 0 0 0 0 1 0 0 0 0 0 0 0
12387 0 0 0 0 1 0 0 0 0 0 0 0
1073745939 0 0 0 0 0 0 0 1 0 0 0 0
4277626595 0 0 0 0 1 0 0 0 0 0 0 0
22686131 0 0 0 0 0 0 0 0 1 0 0 0
4207 0 0 1 0 0 0 0 0 0 0 0 0
4241906403 0 0 0 0 1 0 0 0 0 0 0 0
19 0 0 0 0 0 0 0 1 0 0 0 0
15132211 0 0 0 0 0 0 0 0 1 0 0 0
1081497107 0 0 0 0 0 0 0 1 0 0 0 0
5452435 0 0 0 0 0 0 0 1 0 0 0 0
0 0 0 0 0 0 0 0 0 0 0 0 0
4358375 0 0 0 1 0 0 0 0 0 0 0 0
239 0 0 1 0 0 0 0 0 0 0 0 0
1769442379 0 0 0 0 0 0 0 0 0 0 0 0
15132211 0 0 0 0 0 0 0 0 1 0 0 0
3779918808 0 0 0 0 0 0 0 0 0 0 0 0
0 0 0 0 0 0 0 0 0 0 0 0 0
29183155 0 0 0 0 0 0 0 0 1 0 0 0
1073745939 0 0 0 0 0 0 0 1 0 0 0 0
15132211 0 0 0 0 0 0 0 0 1 0 0 0
273678451 0 0 0 0 0 0 0 0 0 1 0 0
4294198147 0 0 0 0 0 1 0 0 0 0 0 0
16499 0 0 0 0 0 0 0 0 0 1 0 0
1081497107 0 0 0 0 0 0 0 1 0 0 0 0
19 0 0 0 0 0 0 0 1 0 0 0 0
4358375 0 0 0 1 0 0 0 0 0 0 0 0
239 0 0 1 0 0 0 0 0 0 0 0 0
1085628339 0 0 0 0 0 0 0 0 1 0 0 0
273678451 0 0 0 0 0 0 0 0 0 1 0 0
1081497107 0 0 0 0 0 0 0 1 0 0 0 0
1081279155 0 0 0 0 0 0 0 0 1 0 0 0
4358375 0 0 0 1 0 0 0 0 0 0 0 0
4289929875 0 0 0 0 0 0 0 1 0 0 0 0
133588371 0 0 0 0 0 0 0 1 0 0 0 0
4278255891 0 0 0 0 0 0 0 1 0 0 0 0
2184066683 0 0 0 0 0 0 0 0 0 0 0 0
25934643 0 0 0 0 0 0 0 0 1 0 0 0
115 0 0 0 0 0 0 0 0 0 1 1 0
4289929875 0 0 0 0 0 0 0 1 0 0 0 0
4294198147 0 0 0 0 0 1 0 0 0 0 0 0
4207 0 0 1 0 0 0 0 0 0 0 0 0
1048691 0 0 0 0 0 0 0 0 0 1 0 0
5452435 0 0 0 0 0 0 0 1 0 0 0 0
12944691 0 0 0 0 0 0 0 0 1 0 0 0
807403635 0 0 0 0 0 0 0 0 0 1 0 1
305419575 1 0 0 0 0 0 0 0 0 0 0 0
25934643 0 0 0 0 0 0 0 0 1 0 0 0
4199 0 0 0 1 0 0 0 0 0 0 0 0
4131 0 0 0 0 0 0 1 0 0 0 0 0
4887 0 1 0 0 0 0 0 0 0 0 0 0
4278255891 0 0 0 0 0 0 0 1 0 0 0 0
807403635 0 0 0 0 0 0 0 0 0 1 0 1
4294967295 0 0 0 0 0 0 0 0 0 0 0 0
4273278179 0 0 0 0 1 0 0 0 0 0 0 0
2521635589 0 0 0 0 0 0 0 0 0 0 0 0
4199 0 0 0 1 0 0 0 0 0 0 0 0
133588371 0 0 0 0 0 0 0 1 0 0 0 0
805315955 0 0 0 0 0 0 0 0 0 1 0 0
1081279155 0 0 0 0 0 0 0 0 1 0 0 0
25934643 0 0 0 0 0 0 0 0 1 0 0 0
1714914659 0 0 0 0 1 0 0 0 0 0 0 0
789764128 0 0 0 0 0 0 0 0 0 0 0 0
1737073815 0 1 0 0 0 0 0 0 0 0 0 0
2918932415 0 0 0 0 0 0 0 0 0 0 0 0
12323 0 0 0 0 0 0 1 0 0 0 0 0
1081279155 0 0 0 0 0 0 0 0 1 0 0 0
19174451 0 0 0 0 0 0 0 0 1 0 0 0
2031299090 0 0 0 0 0 0 0 0 0 0 0 0
32431667 0 0 0 0 0 0 0 0 1 0 0 0
4294198147 0 0 0 0 0 1 0 0 0 0 0 0
4261581539 0 0 0 0 1 0 0 0 0 0 0 0
4294198147 0 0 0 0 0 1 0 0 0 0 0 0
273678451 0 0 0 0 0 0 0 0 0 1 0 0
4294264083 0 0 0 0 0 0 0 1 0 0 0 0
12323 0 0 0 0 0 0 1 0 0 0 0 0
12323 0 0 0 0 0 0 1 0 0 0 0 0
1199884931 0 0 0 0 0 1 0 0 0 0 0 0
4246240483 0 0 0 0 1 0 0 0 0 0 0 0
4246240483 0 0 0 0 1 0 0 0 0 0 0 0
2105859501 0 0 0 0 0 0 0 0 0 0 0 0
3212547 0 0 0 0 0 1 0 0 0 0 0 0
4273278179 0 0 0 0 1 0 0 0 0 0 0 0
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*/
