// Digital circuit P30.dig as structural Verilog
module P30 (
  input  [3:0] addr,
  input  _1,
  output [31:0] data
);

  ROM #(.AddrBits(4), .Bits(32)) rom_1 (.A(addr), .sel(_1), .D(data));

  // Notes on the sheet:
  //   P30 Boot ROM - Digital task
  //   A ROM part holding the first 16 words of the start-up program sw/lib/crt0.s. You assemble the program and type the machine code in yourself.
  //   Allowed parts: gates + multiplexer/decoder parts + ROM
  //   Do not rename, move or delete the input and output pins.
  //   contents of rom_1 (hex, n*v repeats v):
  //   14137,10113,2b7,2828293,30529073,202b7,3c028293,2a023,40006f,537
  //   ,7050513,8c000ef,34202573,1d4000ef,537,7e50513
endmodule

/* Test case public tests:
addr data
0 82231
1 65811
2 695
3 42107539
4 810717299
5 131767
6 1006797459
7 172067
8 4194415
9 1335
10 117769491
11 146800879
12 874521971
13 490733807
14 1335
15 132449555
*/
