// Digital circuit P34.dig as structural Verilog
module P34 (
  input  dma_req,
  input  [3:0] cpu_addr,
  input  [3:0] cpu_wdata,
  input  cpu_we,
  input  [3:0] cpu_be,
  input  [3:0] dma_addr,
  input  [3:0] dma_wdata,
  input  dma_we,
  output grant,
  output stall,
  output [3:0] addr,
  output [3:0] wdata,
  output we,
  output [3:0] be
);

  Multiplexer #(.Bits(4)) multiplexer_1 (.sel(dma_req), .in_0(cpu_addr), .in_1(dma_addr), .out(addr));
  Multiplexer #(.Bits(4)) multiplexer_2 (.sel(dma_req), .in_0(cpu_wdata), .in_1(dma_wdata), .out(wdata));
  Multiplexer multiplexer_3 (.sel(dma_req), .in_0(cpu_we), .in_1(dma_we), .out(we));
  Multiplexer #(.Bits(4)) multiplexer_4 (.sel(dma_req), .in_0(cpu_be), .in_1(4'b1111), .out(be));

  assign grant = dma_req;
  assign stall = dma_req;

  // Notes on the sheet:
  //   P34 Bus arbiter (CPU vs DMA) - Digital task
  //   4-bit version.
  //   Allowed parts: gates + Multiplexer, Demultiplexer, Decoder, PriorityEncoder
  //   Do not rename, move or delete the input and output pins.
endmodule

/* Test case public tests:
dma_req cpu_addr cpu_wdata cpu_we cpu_be dma_addr dma_wdata dma_we grant stall addr wdata we be
0 0 15 1 8 5 0 0 0 0 0 15 1 8
0 12 8 1 8 9 6 1 0 0 12 8 1 8
1 15 0 1 0 0 10 1 1 1 0 10 1 15
0 12 9 0 7 7 6 1 0 0 12 9 0 7
0 5 0 0 0 15 7 0 0 0 5 0 0 0
0 0 11 0 12 4 15 1 0 0 0 11 0 12
0 2 0 1 15 5 7 0 0 0 2 0 1 15
1 2 10 0 1 13 5 0 1 1 13 5 0 15
0 7 10 1 10 3 7 0 0 0 7 10 1 10
0 1 8 0 3 2 2 1 0 0 1 8 0 3
1 2 11 0 13 0 7 1 1 1 0 7 1 15
1 6 8 1 14 7 15 1 1 1 7 15 1 15
0 7 2 1 15 11 13 0 0 0 7 2 1 15
1 4 4 0 5 13 14 0 1 1 13 14 0 15
0 6 0 0 14 13 5 0 0 0 6 0 0 14
0 1 7 1 10 13 0 0 0 0 1 7 1 10
0 1 5 1 7 7 13 1 0 0 1 5 1 7
1 0 5 0 7 14 5 1 1 1 14 5 1 15
1 13 15 0 4 8 8 0 1 1 8 8 0 15
0 7 0 0 15 8 5 0 0 0 7 0 0 15
1 11 5 0 9 2 15 1 1 1 2 15 1 15
0 0 14 0 1 14 15 0 0 0 0 14 0 1
0 2 8 1 11 13 12 0 0 0 2 8 1 11
1 9 15 0 1 1 5 1 1 1 1 5 1 15
0 3 12 1 5 4 7 0 0 0 3 12 1 5
1 14 10 0 15 2 7 0 1 1 2 7 0 15
0 15 4 0 2 15 8 0 0 0 15 4 0 2
1 5 11 1 14 8 0 0 1 1 8 0 0 15
0 12 1 1 15 11 5 0 0 0 12 1 1 15
1 2 7 1 14 2 7 0 1 1 2 7 0 15
0 10 14 1 12 2 8 1 0 0 10 14 1 12
1 4 0 0 10 8 8 0 1 1 8 8 0 15
1 12 7 1 2 1 15 0 1 1 1 15 0 15
1 5 15 0 12 0 5 1 1 1 0 5 1 15
0 10 0 1 5 8 8 0 0 0 10 0 1 5
1 0 4 1 0 1 8 1 1 1 1 8 1 15
1 7 9 0 7 0 10 0 1 1 0 10 0 15
0 0 14 0 13 15 15 1 0 0 0 14 0 13
1 10 7 0 4 4 15 0 1 1 4 15 0 15
1 0 11 1 7 8 0 1 1 1 8 0 1 15
0 12 1 0 8 7 2 0 0 0 12 1 0 8
0 2 15 0 15 15 8 1 0 0 2 15 0 15
1 0 3 0 13 3 13 1 1 1 3 13 1 15
1 8 3 0 11 11 11 0 1 1 11 11 0 15
0 5 0 1 15 14 0 0 0 0 5 0 1 15
0 13 5 0 6 0 2 0 0 0 13 5 0 6
1 14 8 0 7 12 11 1 1 1 12 11 1 15
0 8 1 0 0 0 0 1 0 0 8 1 0 0
1 7 0 0 1 2 9 0 1 1 2 9 0 15
1 3 12 0 1 0 15 1 1 1 0 15 1 15
0 8 4 1 1 0 15 0 0 0 8 4 1 1
1 13 0 1 6 1 7 0 1 1 1 7 0 15
0 7 6 1 14 0 13 0 0 0 7 6 1 14
0 7 10 0 8 0 7 1 0 0 7 10 0 8
0 3 8 0 12 7 12 0 0 0 3 8 0 12
0 0 12 0 1 15 11 1 0 0 0 12 0 1
0 7 7 0 6 2 15 0 0 0 7 7 0 6
0 3 6 1 9 15 6 0 0 0 3 6 1 9
1 3 7 0 11 11 11 0 1 1 11 11 0 15
0 8 15 1 3 13 0 0 0 0 8 15 1 3
1 0 2 1 3 12 15 1 1 1 12 15 1 15
0 7 14 0 8 0 3 1 0 0 7 14 0 8
0 12 5 0 15 12 3 0 0 0 12 5 0 15
0 6 4 1 15 9 15 0 0 0 6 4 1 15
0 15 0 1 14 14 11 0 0 0 15 0 1 14
0 6 9 1 15 0 1 0 0 0 6 9 1 15
1 0 8 0 8 8 7 1 1 1 8 7 1 15
0 13 12 0 6 0 5 1 0 0 13 12 0 6
1 15 10 1 8 13 0 0 1 1 13 0 0 15
0 13 0 0 0 14 13 1 0 0 13 0 0 0
0 0 13 1 0 6 0 1 0 0 0 13 1 0
0 15 9 1 13 12 8 1 0 0 15 9 1 13
0 11 14 0 11 15 7 1 0 0 11 14 0 11
0 4 0 1 15 4 10 1 0 0 4 0 1 15
0 5 4 1 9 11 4 0 0 0 5 4 1 9
0 11 10 1 15 0 10 0 0 0 11 10 1 15
0 10 14 0 2 5 0 1 0 0 10 14 0 2
1 0 0 0 2 1 0 1 1 1 1 0 1 15
1 11 0 0 7 15 11 0 1 1 15 11 0 15
0 2 2 0 15 1 6 0 0 0 2 2 0 15
1 3 11 0 2 6 11 1 1 1 6 11 1 15
0 6 8 0 15 12 4 0 0 0 6 8 0 15
0 15 2 0 13 4 5 1 0 0 15 2 0 13
0 9 10 1 14 8 13 0 0 0 9 10 1 14
1 14 11 0 6 9 14 0 1 1 9 14 0 15
1 0 3 0 4 14 8 1 1 1 14 8 1 15
1 1 0 0 2 8 5 0 1 1 8 5 0 15
1 3 1 1 11 14 7 1 1 1 14 7 1 15
0 15 0 1 5 5 0 0 0 0 15 0 1 5
0 12 6 1 15 15 9 0 0 0 12 6 1 15
1 14 12 1 7 4 8 1 1 1 4 8 1 15
0 7 2 1 7 8 6 1 0 0 7 2 1 7
0 0 11 1 5 4 7 0 0 0 0 11 1 5
0 12 11 1 11 5 11 1 0 0 12 11 1 11
0 9 14 1 15 1 13 1 0 0 9 14 1 15
0 3 12 1 11 11 0 0 0 0 3 12 1 11
1 0 0 1 11 5 4 1 1 1 5 4 1 15
1 8 5 0 4 11 0 1 1 1 11 0 1 15
1 8 0 0 11 10 12 0 1 1 10 12 0 15
0 7 7 0 7 8 5 1 0 0 7 7 0 7
1 4 8 1 0 9 13 1 1 1 9 13 1 15
0 3 7 0 0 8 13 1 0 0 3 7 0 0
1 14 8 0 8 15 3 0 1 1 15 3 0 15
0 13 9 1 0 6 8 1 0 0 13 9 1 0
0 7 0 0 1 11 7 0 0 0 7 0 0 1
1 8 6 0 10 0 1 0 1 1 0 1 0 15
0 6 0 0 3 8 11 0 0 0 6 0 0 3
0 7 5 0 8 6 11 1 0 0 7 5 0 8
0 7 9 0 4 14 7 0 0 0 7 9 0 4
0 13 7 0 11 11 0 1 0 0 13 7 0 11
0 8 7 1 8 4 5 0 0 0 8 7 1 8
0 4 8 1 6 3 7 0 0 0 4 8 1 6
0 11 11 1 1 15 7 1 0 0 11 11 1 1
0 7 0 0 4 15 14 0 0 0 7 0 0 4
0 10 8 0 0 8 10 1 0 0 10 8 0 0
1 15 0 1 8 15 9 0 1 1 15 9 0 15
0 10 0 1 6 5 15 1 0 0 10 0 1 6
1 5 0 1 3 3 0 1 1 1 3 0 1 15
1 7 15 1 12 0 15 1 1 1 0 15 1 15
0 4 2 0 0 8 11 0 0 0 4 2 0 0
0 15 5 1 14 8 12 1 0 0 15 5 1 14
1 4 7 0 2 14 6 0 1 1 14 6 0 15
1 10 7 0 4 6 0 1 1 1 6 0 1 15
1 15 6 1 13 5 15 1 1 1 5 15 1 15
0 8 8 0 6 8 8 1 0 0 8 8 0 6
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*/
