// Digital circuit P37.dig as structural Verilog
module P37 (
  input  clk,
  input  rst,
  input  we,
  input  [7:0] wdata,
  input  trap,
  input  mret,
  input  set_mie,
  output [7:0] mtvec,
  output mie,
  output mpie
);

  wire multiplexer_3_out, multiplexer_5_out, multiplexer_6_out, multiplexer_8_out, multiplexer_9_out,
       multiplexer_10_out, multiplexer_11_out;
  wire [7:0] multiplexer_1_out, multiplexer_2_out, multiplexer_4_out, multiplexer_7_out;

  D_FF #(.Bits(8)) u_mtvec (.D(multiplexer_7_out), .C(clk), .Q(mtvec));  // open: nQ
  D_FF u_mpie (.D(multiplexer_10_out), .C(clk), .Q(mpie));  // open: nQ
  D_FF u_mie (.D(multiplexer_11_out), .C(clk), .Q(mie));  // open: nQ
  Multiplexer #(.Bits(8)) multiplexer_1 (.sel(we), .in_0(mtvec), .in_1(wdata), .out(multiplexer_1_out));
  Multiplexer #(.Bits(8)) multiplexer_2 (.sel(mret), .in_0(multiplexer_1_out), .in_1(mtvec), .out(multiplexer_2_out));
  Multiplexer multiplexer_3 (.sel(set_mie), .in_0(mie), .in_1(1'b1), .out(multiplexer_3_out));
  Multiplexer #(.Bits(8)) multiplexer_4 (.sel(trap), .in_0(multiplexer_2_out), .in_1(mtvec), .out(multiplexer_4_out));
  Multiplexer multiplexer_5 (.sel(mret), .in_0(mpie), .in_1(1'b1), .out(multiplexer_5_out));
  Multiplexer multiplexer_6 (.sel(mret), .in_0(multiplexer_3_out), .in_1(mpie), .out(multiplexer_6_out));
  Multiplexer #(.Bits(8)) multiplexer_7 (
    .sel(rst), .in_0(multiplexer_4_out), .in_1({8{1'b0}}), .out(multiplexer_7_out));
  Multiplexer multiplexer_8 (.sel(trap), .in_0(multiplexer_5_out), .in_1(mie), .out(multiplexer_8_out));
  Multiplexer multiplexer_9 (.sel(trap), .in_0(multiplexer_6_out), .in_1(1'b0), .out(multiplexer_9_out));
  Multiplexer multiplexer_10 (.sel(rst), .in_0(multiplexer_8_out), .in_1(1'b0), .out(multiplexer_10_out));
  Multiplexer multiplexer_11 (.sel(rst), .in_0(multiplexer_9_out), .in_1(1'b0), .out(multiplexer_11_out));

  // Notes on the sheet:
  //   clk: Hz: 1
  //   P37 Control and status registers - Digital task
  //   Scaled: an 8-bit mtvec register and the MIE/MPIE flip-flops with trap and mret behaviour.
  //   Allowed parts: gates + multiplexer/decoder parts + flip-flops
  //   Do not rename, move or delete the input and output pins.
endmodule

/* Test case public tests:
clk rst we wdata trap mret set_mie mtvec mie mpie
C 1 1 128 0 0 1 0 0 0
C 0 0 227 1 0 1 0 0 0
C 0 0 176 0 1 0 0 0 1
C 0 1 26 0 0 1 26 1 1
C 0 0 0 1 1 1 26 0 1
C 0 0 2 1 1 1 26 0 0
C 0 0 41 0 0 1 26 1 0
C 0 0 9 0 1 0 26 0 1
C 0 0 13 1 0 0 26 0 0
C 0 0 11 0 0 1 26 1 0
C 0 0 25 0 1 1 26 0 1
C 0 0 2 0 1 0 26 1 1
C 0 0 116 1 0 1 26 0 1
C 0 0 185 1 1 1 26 0 0
C 0 1 95 1 0 1 26 0 0
C 0 0 255 0 1 0 26 0 1
C 0 1 108 1 1 1 26 0 0
C 0 1 76 1 0 0 26 0 0
C 0 1 255 0 0 0 255 0 0
C 0 1 129 0 1 0 255 0 1
C 0 1 0 1 1 1 255 0 0
C 0 0 83 1 1 0 255 0 0
C 0 1 15 0 0 1 15 1 0
C 0 0 231 1 0 0 15 0 1
C 0 0 128 0 0 1 15 1 1
C 0 1 34 1 0 0 15 0 1
C 0 0 60 1 0 1 15 0 0
C 0 1 10 0 1 1 15 0 1
C 0 1 30 1 1 0 15 0 0
C 0 0 245 0 0 0 15 0 0
C 0 0 4 0 1 1 15 0 1
C 0 0 167 0 1 1 15 1 1
C 0 0 128 1 0 0 15 0 1
C 0 0 0 0 1 1 15 1 1
C 0 1 30 0 1 1 15 1 1
C 0 0 127 1 0 0 15 0 1
C 0 0 27 0 0 0 15 0 1
C 0 0 137 0 0 0 15 0 1
C 0 1 135 1 0 1 15 0 0
C 0 0 23 0 1 1 15 0 1
C 0 0 192 1 1 1 15 0 0
C 0 1 8 0 0 0 8 0 0
C 0 0 92 0 0 0 8 0 0
C 0 0 127 0 0 0 8 0 0
C 0 1 118 0 1 0 8 0 1
C 0 0 127 1 1 0 8 0 0
C 0 1 128 1 0 0 8 0 0
C 0 0 41 1 1 1 8 0 0
C 0 0 17 1 1 0 8 0 0
C 0 0 48 1 1 0 8 0 0
C 0 0 128 1 1 1 8 0 0
C 0 1 51 1 1 1 8 0 0
C 0 1 9 1 1 0 8 0 0
C 0 0 255 0 1 1 8 0 1
C 0 1 15 0 1 0 8 1 1
C 0 1 128 0 0 1 128 1 1
C 0 1 79 0 1 1 128 1 1
C 0 0 89 1 1 1 128 0 1
C 0 1 255 1 1 0 128 0 0
C 0 0 14 0 0 1 128 1 0
C 0 1 21 1 0 0 128 0 1
C 0 0 4 0 1 1 128 1 1
C 0 1 114 0 0 0 114 1 1
C 0 0 2 1 1 1 114 0 1
C 0 1 176 1 0 0 114 0 0
C 0 0 146 1 0 0 114 0 0
C 0 0 128 0 1 1 114 0 1
C 0 1 0 0 0 0 0 0 1
C 0 0 0 0 1 1 0 1 1
C 0 1 26 0 1 1 0 1 1
C 0 0 127 1 0 0 0 0 1
C 0 1 218 1 1 1 0 0 0
C 0 0 9 0 1 1 0 0 1
C 0 1 5 1 0 1 0 0 0
C 1 1 56 1 1 1 0 0 0
C 0 0 128 0 1 1 0 0 1
C 0 1 90 1 1 0 0 0 0
C 0 0 127 1 0 0 0 0 0
C 0 0 7 0 1 1 0 0 1
C 1 0 21 1 1 1 0 0 0
C 0 0 172 0 1 0 0 0 1
C 0 0 15 0 1 0 0 1 1
C 0 1 194 0 0 0 194 1 1
C 0 0 61 0 0 0 194 1 1
C 0 1 127 1 1 0 194 0 1
C 0 0 19 1 0 0 194 0 0
C 0 0 199 1 1 1 194 0 0
C 0 1 1 1 0 0 194 0 0
C 0 1 225 1 1 1 194 0 0
C 0 0 25 1 0 1 194 0 0
C 0 0 160 0 0 0 194 0 0
C 0 1 28 1 1 1 194 0 0
C 0 1 29 0 1 0 194 0 1
C 0 1 152 1 1 1 194 0 0
C 0 0 255 0 0 0 194 0 0
C 0 1 64 1 0 0 194 0 0
C 0 1 7 1 1 0 194 0 0
C 0 1 21 0 1 0 194 0 1
C 0 0 200 0 0 0 194 0 1
C 0 1 255 1 1 0 194 0 0
C 0 0 173 0 1 1 194 0 1
C 0 0 74 1 0 1 194 0 0
C 0 1 165 0 1 1 194 0 1
C 0 0 120 0 0 1 194 1 1
C 0 0 23 0 1 1 194 1 1
C 1 0 0 1 0 1 0 0 0
C 0 0 64 1 0 0 0 0 0
C 0 1 103 1 0 0 0 0 0
C 0 0 0 1 1 1 0 0 0
C 0 1 120 1 1 0 0 0 0
C 0 0 0 1 1 1 0 0 0
C 0 0 127 0 0 0 0 0 0
C 0 1 128 0 1 1 0 0 1
C 0 0 255 1 1 1 0 0 0
C 0 1 229 0 0 0 229 0 0
C 0 1 127 0 1 0 229 0 1
C 0 0 177 1 1 1 229 0 0
C 0 1 82 1 0 1 229 0 0
C 0 0 0 1 0 1 229 0 0
C 0 0 36 1 0 0 229 0 0
C 0 1 6 0 0 1 6 1 0
C 0 1 87 1 0 0 6 0 1
C 0 1 128 0 1 1 6 1 1
C 0 1 214 0 1 0 6 1 1
C 0 0 126 1 1 1 6 0 1
C 0 1 128 1 0 1 6 0 0
C 0 1 45 0 1 1 6 0 1
C 0 0 0 1 0 0 6 0 0
C 0 1 31 1 0 1 6 0 0
C 0 1 18 1 1 0 6 0 0
C 0 1 18 1 0 0 6 0 0
C 0 1 56 1 1 1 6 0 0
C 0 0 106 1 0 0 6 0 0
C 0 1 31 1 0 0 6 0 0
C 0 1 0 0 1 1 6 0 1
C 0 0 23 0 1 1 6 1 1
C 0 1 79 1 0 0 6 0 1
C 0 0 255 1 0 1 6 0 0
C 0 0 153 0 0 1 6 1 0
C 0 1 245 0 1 0 6 0 1
C 0 1 47 1 0 0 6 0 0
C 0 0 0 1 1 0 6 0 0
C 0 0 0 0 0 1 6 1 0
C 0 0 118 1 0 1 6 0 1
C 0 1 142 1 0 0 6 0 0
C 0 0 128 1 1 0 6 0 0
C 0 0 126 0 0 0 6 0 0
C 0 0 255 1 0 1 6 0 0
C 0 0 127 0 0 1 6 1 0
C 0 0 119 0 0 0 6 1 0
C 0 0 88 1 1 1 6 0 1
C 0 0 229 1 0 0 6 0 0
C 0 1 128 0 0 1 128 1 0
C 0 1 50 0 0 1 50 1 0
C 0 0 0 1 1 1 50 0 1
C 0 1 77 1 1 1 50 0 0
C 0 1 28 0 0 1 28 1 0
C 0 1 128 1 0 0 28 0 1
C 0 1 206 0 0 1 206 1 1
C 0 1 223 0 0 0 223 1 1
*/
