// Digital circuit P43.dig as structural Verilog
module P43 (
  input  clk,
  input  rst,
  input  we,
  input  [1:0] ridx,
  input  [7:0] wdata,
  input  [7:0] buttons,
  output [7:0] rdata,
  output [7:0] leds
);

  wire and_1_out, decoder_1_out_0;
  wire [7:0] multiplexer_1_out, multiplexer_2_out;

  Decoder #(.Selector_Bits(2)) decoder_1 (.sel(ridx), .out_0(decoder_1_out_0));  // open: out_1, out_2, out_3
  Multiplexer #(.Bits(8)) multiplexer_1 (.sel(and_1_out), .in_0(leds), .in_1(wdata), .out(multiplexer_1_out));
  and and_1 (and_1_out, we, decoder_1_out_0);
  Multiplexer #(.Bits(8)) multiplexer_2 (
    .sel(rst), .in_0(multiplexer_1_out), .in_1({8{1'b0}}), .out(multiplexer_2_out));
  D_FF #(.Bits(8)) d_ff_1 (.D(multiplexer_2_out), .C(clk), .Q(leds));  // open: nQ
  Multiplexer #(.Bits(8), .Selector_Bits(2)) multiplexer_3 (
    .sel(ridx), .in_0(leds), .in_1({8{1'b0}}), .in_2(buttons), .in_3({8{1'b0}}), .out(rdata));

  // Notes on the sheet:
  //   clk: Hz: 1
  //   P43 LEDs, display register and buttons - Digital task
  //   8-bit LED register plus the read multiplexer.
  //   Allowed parts: gates + multiplexer/decoder parts + flip-flops
  //   Do not rename, move or delete the input and output pins.
endmodule

/* Test case public tests:
clk rst we ridx wdata buttons rdata leds
C 1 1 3 27 121 0 0
C 0 0 2 223 29 29 0
C 0 1 1 255 0 0 0
C 0 1 2 49 60 60 0
C 0 0 1 226 127 0 0
C 0 0 1 255 0 0 0
C 0 0 1 128 127 0 0
C 0 1 0 187 33 187 187
C 0 0 1 127 255 0 187
C 0 1 2 66 40 40 187
C 0 1 1 6 255 0 187
C 0 1 2 255 0 0 187
C 0 0 2 127 115 115 187
C 0 0 0 0 179 187 187
C 0 0 0 255 91 187 187
C 0 0 2 43 34 34 187
C 0 0 3 0 24 0 187
C 0 1 3 105 128 0 187
C 0 1 0 255 7 255 255
C 0 1 2 27 120 120 255
C 1 1 1 0 96 0 0
C 0 0 3 14 255 0 0
C 0 1 0 158 5 158 158
C 0 1 0 0 102 0 0
C 0 0 2 6 64 64 0
C 0 1 2 228 117 117 0
C 0 1 0 6 220 6 6
C 0 1 3 0 227 0 6
C 0 1 0 73 27 73 73
C 0 1 0 127 205 127 127
C 0 1 1 105 163 0 127
C 0 1 0 0 193 0 0
C 0 1 2 202 229 229 0
C 0 0 1 127 16 0 0
C 0 0 1 209 127 0 0
C 0 1 2 21 127 127 0
C 0 1 2 101 28 28 0
C 0 1 0 91 252 91 91
C 0 0 1 128 12 0 91
C 0 1 1 16 112 0 91
C 0 1 0 36 0 36 36
C 0 1 1 79 127 0 36
C 0 1 2 127 0 0 36
C 0 1 3 45 176 0 36
C 0 0 3 21 210 0 36
C 0 0 3 74 221 0 36
C 0 0 2 16 211 211 36
C 0 0 3 146 37 0 36
C 0 1 2 45 128 128 36
C 0 0 2 127 38 38 36
C 0 0 3 13 42 0 36
C 0 0 0 235 216 36 36
C 0 0 1 227 128 0 36
C 0 1 0 21 119 21 21
C 0 1 2 219 127 127 21
C 0 1 2 195 120 120 21
C 0 0 3 128 233 0 21
C 0 0 0 95 230 21 21
C 0 1 0 3 219 3 3
C 0 0 2 160 127 127 3
C 0 1 3 177 182 0 3
C 0 1 1 187 44 0 3
C 0 0 2 118 74 74 3
C 0 0 1 109 0 0 3
C 0 0 1 128 6 0 3
C 0 0 3 128 127 0 3
C 0 1 1 47 255 0 3
C 0 1 2 14 106 106 3
C 0 0 1 0 138 0 3
C 0 1 0 229 76 229 229
C 0 1 3 255 127 0 229
C 0 1 1 24 2 0 229
C 0 0 0 80 127 229 229
C 0 1 0 16 127 16 16
C 0 1 3 21 255 0 16
C 0 1 2 128 108 108 16
C 0 0 2 127 133 133 16
C 0 0 3 44 135 0 16
C 0 1 3 127 152 0 16
C 0 1 3 21 128 0 16
C 0 0 1 14 243 0 16
C 0 1 2 96 169 169 16
C 0 0 2 218 11 11 16
C 0 1 0 226 54 226 226
C 0 0 2 128 138 138 226
C 0 0 0 11 50 226 226
C 0 0 3 103 49 0 226
C 0 0 3 222 4 0 226
C 0 1 0 209 244 209 209
C 0 0 3 200 0 0 209
C 0 1 1 224 132 0 209
C 0 1 0 17 193 17 17
C 0 1 3 5 209 0 17
C 0 1 0 0 55 0 0
C 0 0 1 127 120 0 0
C 0 1 1 106 216 0 0
C 0 1 0 0 128 0 0
C 0 1 0 255 11 255 255
C 0 0 3 255 14 0 255
C 0 1 1 6 165 0 255
C 0 0 3 223 145 0 255
C 0 0 0 255 108 255 255
C 0 1 3 4 136 0 255
C 0 1 3 2 70 0 255
C 0 1 2 30 124 124 255
C 0 1 3 115 255 0 255
C 0 0 2 128 153 153 255
C 0 1 2 231 60 60 255
C 0 0 2 9 0 0 255
C 0 1 1 0 163 0 255
C 0 1 3 16 5 0 255
C 0 0 1 90 199 0 255
C 0 0 1 23 0 0 255
C 0 1 0 31 24 31 31
C 0 1 3 224 197 0 31
C 0 1 2 128 128 128 31
C 0 0 0 146 0 31 31
C 0 0 1 0 65 0 31
C 0 1 0 6 25 6 6
C 0 1 0 221 7 221 221
C 0 0 0 236 190 221 221
C 0 1 1 69 128 0 221
C 0 0 1 84 152 0 221
C 0 0 0 207 127 221 221
C 1 1 3 149 0 0 0
C 0 0 3 127 5 0 0
C 0 1 1 178 172 0 0
C 0 1 0 26 26 26 26
C 0 0 0 0 255 26 26
C 0 0 1 199 70 0 26
C 0 0 1 22 127 0 26
C 0 0 1 53 127 0 26
C 0 1 1 21 255 0 26
C 0 1 3 45 60 0 26
C 0 1 3 6 10 0 26
C 0 1 0 22 17 22 22
C 0 0 0 2 230 22 22
C 0 0 3 127 34 0 22
C 0 1 2 83 21 21 22
C 0 1 2 121 8 8 22
C 0 0 1 41 127 0 22
C 0 0 3 20 5 0 22
C 0 0 0 123 197 22 22
C 0 0 3 0 9 0 22
C 0 1 2 0 224 224 22
C 0 1 0 34 230 34 34
C 0 0 3 91 16 0 34
C 0 0 3 128 53 0 34
C 0 1 0 255 0 255 255
C 0 0 2 246 49 49 255
C 0 1 0 128 8 128 128
C 0 0 3 0 239 0 128
C 0 0 3 15 211 0 128
C 0 1 1 8 127 0 128
C 0 1 1 255 241 0 128
C 0 1 2 64 200 200 128
C 0 1 0 16 255 16 16
C 0 1 1 154 0 0 16
C 0 1 2 29 151 151 16
C 0 0 3 15 53 0 16
*/
