// Digital circuit P46.dig as structural Verilog
module P46 (
  input  clk,
  input  rst,
  input  en,
  input  load,
  input  [7:0] d,
  input  [7:0] cmp,
  input  clr,
  output [7:0] count,
  output match
);

  // And and_1 is placed but not wired

  // Notes on the sheet:
  //   clk: Hz: 1
  //   P46 Timer - Digital task
  //   8-bit counter with load, an 8-bit comparator and the sticky match flag.
  //   Allowed parts: all of the above + Add, Sub, Comparator, Neg
  //   Do not rename, move or delete the input and output pins.
endmodule

/* Test case public tests:
clk rst en load d cmp clr count match
C 1 1 0 201 1 0 0 0
C 0 0 0 13 128 1 0 0
C 0 0 0 219 247 0 0 0
C 0 1 0 255 243 1 1 0
C 0 0 1 63 0 1 63 0
C 0 0 1 145 128 0 145 0
C 0 1 1 204 14 0 204 0
C 0 1 1 64 215 1 64 0
C 0 1 0 132 211 1 65 0
C 0 0 1 34 94 1 34 0
C 0 0 1 241 215 1 241 0
C 0 0 0 118 128 0 241 0
C 0 1 1 24 18 0 24 0
C 0 1 0 27 26 1 25 0
C 0 0 0 233 55 1 25 0
C 0 1 1 127 42 0 127 0
C 0 0 1 20 97 0 20 0
C 0 1 0 32 131 1 21 0
C 0 1 1 86 170 0 86 0
C 1 0 1 21 255 1 0 0
C 0 1 1 94 16 1 94 0
C 0 0 1 192 161 0 192 0
C 0 1 0 224 0 0 193 0
C 0 0 1 255 180 1 255 0
C 0 0 0 210 127 0 255 0
C 0 0 0 255 16 0 255 0
C 0 0 1 4 25 1 4 0
C 0 1 0 86 127 1 5 0
C 0 1 1 11 9 1 11 0
C 0 1 0 253 255 0 12 0
C 0 1 0 249 18 0 13 0
C 0 1 1 57 4 0 57 0
C 0 1 1 155 92 0 155 0
C 0 0 0 28 23 0 155 0
C 0 0 0 255 127 1 155 0
C 0 1 0 109 173 1 156 0
C 0 1 0 12 2 1 157 0
C 0 0 0 255 0 0 157 0
C 0 0 0 255 30 0 157 0
C 0 1 1 96 166 1 96 0
C 0 0 1 255 47 0 255 0
C 0 0 0 192 0 0 255 0
C 0 1 1 118 184 0 118 0
C 0 0 1 13 187 1 13 0
C 0 1 0 127 239 1 14 0
C 0 1 1 254 18 1 254 0
C 0 1 0 185 117 1 255 0
C 0 1 1 127 50 0 127 0
C 0 1 0 29 255 0 128 0
C 0 1 0 20 0 1 129 0
C 0 0 0 216 0 0 129 0
C 0 0 0 128 45 0 129 0
C 0 0 1 153 229 0 153 0
C 0 1 0 17 172 0 154 0
C 0 0 0 115 227 1 154 0
C 0 0 0 254 30 0 154 0
C 0 1 0 128 127 0 155 0
C 0 1 1 91 179 1 91 0
C 0 1 1 0 127 1 0 0
C 0 0 1 0 190 0 0 0
C 0 1 0 204 32 0 1 0
C 0 1 1 142 27 1 142 0
C 0 1 1 2 127 1 2 0
C 0 0 1 73 7 0 73 0
C 0 0 1 201 127 1 201 0
C 0 1 0 191 173 0 202 0
C 0 0 1 45 128 1 45 0
C 0 0 1 33 182 0 33 0
C 0 1 1 20 6 0 20 0
C 0 1 1 161 19 1 161 0
C 0 1 1 193 193 0 193 0
C 0 0 1 127 185 0 127 0
C 0 1 0 197 255 0 128 0
C 0 1 1 0 255 0 0 0
C 0 0 0 0 30 0 0 0
C 0 0 0 132 30 0 0 0
C 0 1 0 188 185 0 1 0
C 0 1 1 248 45 1 248 0
C 0 0 0 56 128 0 248 0
C 0 0 1 107 55 0 107 0
C 0 1 1 128 24 1 128 0
C 0 0 0 58 84 1 128 0
C 0 0 1 128 0 0 128 0
C 0 1 1 0 128 0 0 1
C 0 1 0 127 127 0 1 1
C 0 0 1 226 112 1 226 0
C 0 0 1 122 127 0 122 0
C 0 0 0 255 92 1 122 0
C 0 0 1 0 251 0 0 0
C 0 1 1 139 11 0 139 0
C 0 1 1 31 127 1 31 0
C 0 0 0 14 3 0 31 0
C 0 1 0 197 112 1 32 0
C 0 0 1 1 136 1 1 0
C 0 0 0 128 5 1 1 0
C 0 1 0 113 14 0 2 0
C 0 0 0 219 229 0 2 0
C 0 1 0 100 31 0 3 0
C 0 1 0 127 128 1 4 0
C 0 0 0 27 143 1 4 0
C 0 0 0 13 128 0 4 0
C 0 0 0 65 128 1 4 0
C 0 1 0 6 255 1 5 0
C 0 0 1 233 255 1 233 0
C 0 1 1 127 218 0 127 0
C 0 1 1 31 31 1 31 0
C 0 1 0 71 222 0 32 0
C 0 0 1 72 25 1 72 0
C 0 0 1 5 112 1 5 0
C 0 0 0 219 255 0 5 0
C 0 0 1 0 47 1 0 0
C 0 1 1 187 128 0 187 0
C 0 0 0 141 238 1 187 0
C 0 1 0 127 103 0 188 0
C 0 0 0 19 183 0 188 0
C 0 1 1 255 8 0 255 0
C 0 0 0 195 55 1 255 0
C 0 1 0 218 210 0 0 0
C 0 0 0 249 78 1 0 0
C 0 0 0 4 83 1 0 0
C 0 0 0 117 11 0 0 0
C 0 0 0 128 3 1 0 0
C 0 0 1 74 127 1 74 0
C 0 0 1 255 115 0 255 0
C 0 0 1 128 26 1 128 0
C 0 1 1 11 17 1 11 0
C 0 0 1 4 127 0 4 0
C 0 0 1 8 2 1 8 0
C 0 1 1 40 255 1 40 0
C 0 0 0 25 35 0 40 0
C 0 1 0 5 0 0 41 0
C 0 1 0 169 0 0 42 0
C 0 0 0 0 143 0 42 0
C 0 1 1 99 0 0 99 0
C 0 0 0 28 105 1 99 0
C 0 1 0 171 29 0 100 0
C 0 1 0 156 255 1 101 0
C 1 0 0 13 250 0 0 0
C 0 1 0 19 127 0 1 0
C 0 0 0 40 9 1 1 0
C 0 0 0 22 0 0 1 0
C 0 0 1 31 173 0 31 0
C 0 0 0 0 215 1 31 0
C 0 0 1 249 255 1 249 0
C 0 1 0 197 242 1 250 0
C 0 0 1 0 5 1 0 0
C 0 1 0 22 128 0 1 0
C 0 1 1 30 20 1 30 0
C 0 0 1 22 57 1 22 0
C 0 1 1 223 112 0 223 0
C 0 0 0 58 255 1 223 0
C 0 1 0 8 51 0 224 0
C 0 1 0 127 88 0 225 0
C 0 1 1 128 106 1 128 0
C 0 0 0 0 146 1 128 0
C 0 0 1 194 90 1 194 0
C 0 0 0 126 127 1 194 0
C 0 1 0 127 127 1 195 0
C 0 0 0 18 112 1 195 0
C 0 1 0 33 2 1 196 0
*/
