// Digital circuit P51.dig as structural Verilog
module P51 (
  input  [7:0] a,
  input  [7:0] b,
  output [7:0] sum,
  output [7:0] max
);

  wire comparator_1_gt, comparator_2_gt;

  Add #(.Bits(4)) add_1 (.a(a[3:0]), .b(b[3:0]), .c_i(1'b0), .s(sum[3:0]));  // open: c_o
  Add #(.Bits(4)) add_2 (.a(a[7:4]), .b(b[7:4]), .c_i(1'b0), .s(sum[7:4]));  // open: c_o
  Comparator #(.Bits(4)) comparator_1 (.a(a[3:0]), .b(b[3:0]), .gt(comparator_1_gt));  // open: eq, lt
  Comparator #(.Bits(4)) comparator_2 (.a(a[7:4]), .b(b[7:4]), .gt(comparator_2_gt));  // open: eq, lt
  Multiplexer #(.Bits(4)) multiplexer_1 (.sel(comparator_1_gt), .in_0(b[3:0]), .in_1(a[3:0]), .out(max[3:0]));
  Multiplexer #(.Bits(4)) multiplexer_2 (.sel(comparator_2_gt), .in_0(b[7:4]), .in_1(a[7:4]), .out(max[7:4]));

  // Notes on the sheet:
  //   P51 Four-lane vector unit (mini GPU) - Digital task
  //   2 lanes of 4 bits: per-lane adders and comparators (Add/Comparator parts allowed).
  //   Allowed parts: all of the above + Add, Sub, Comparator, Neg
  //   Do not rename, move or delete the input and output pins.
endmodule

/* Test case public tests:
a b sum max
0 255 255 255
141 0 141 141
18 60 78 60
109 255 92 255
31 128 159 143
94 12 90 94
128 238 110 238
218 247 193 250
147 253 128 253
230 228 202 230
127 127 238 127
20 108 112 108
28 20 32 28
0 99 99 99
10 33 43 42
231 128 103 231
159 51 194 159
6 211 217 214
201 52 253 201
127 189 44 191
119 85 204 119
62 79 125 79
146 45 191 157
128 197 69 197
112 107 219 123
123 121 228 123
63 232 23 239
187 13 184 189
31 227 242 239
29 61 74 61
82 89 171 89
128 4 132 132
18 0 18 18
129 0 129 129
69 24 93 72
128 70 198 134
12 149 145 156
44 231 3 236
251 127 106 255
0 6 6 6
255 74 57 255
1 0 1 1
221 196 145 221
216 17 233 216
0 190 190 190
2 255 241 255
255 19 2 255
79 238 45 239
167 103 14 167
26 28 38 28
0 8 8 8
162 161 67 162
124 9 117 124
50 248 42 248
127 33 144 127
0 45 45 45
127 62 173 127
141 17 158 141
7 237 228 237
255 127 110 255
143 0 143 143
162 255 145 255
127 188 43 191
9 127 120 127
127 185 40 191
128 160 32 160
128 75 203 139
241 202 187 250
4 8 12 8
35 101 136 101
157 168 53 173
158 255 141 255
127 140 251 143
167 191 86 191
62 132 178 142
255 255 238 255
1 13 14 13
57 166 223 169
16 0 16 16
127 2 113 127
24 242 10 248
25 53 78 57
70 0 70 70
24 127 135 127
213 227 184 229
96 96 192 96
19 128 147 131
12 31 27 31
13 0 13 13
31 193 208 207
159 245 132 255
154 22 160 154
221 245 194 253
31 127 142 127
143 128 15 143
12 20 16 28
74 157 215 157
191 225 144 239
255 17 0 255
128 247 119 247
30 0 30 30
37 117 154 117
216 216 160 216
22 128 150 134
146 255 129 255
127 7 118 127
211 128 83 211
205 207 140 207
100 66 166 100
151 169 48 169
128 132 4 132
12 127 123 127
59 128 187 139
127 147 2 159
1 104 105 104
255 128 127 255
222 47 253 223
107 255 90 255
207 120 55 207
128 147 19 147
0 30 30 30
162 31 177 175
103 13 100 109
255 128 127 255
31 128 159 143
128 18 146 130
59 255 42 255
23 4 27 23
128 125 253 141
46 113 159 126
18 235 253 235
239 2 225 239
52 5 57 53
0 0 0 0
55 165 220 167
128 62 190 142
128 94 222 142
167 37 204 167
179 202 125 202
16 87 103 87
255 0 255 255
203 240 187 251
132 148 24 148
153 128 25 153
0 255 255 255
101 185 30 185
168 250 146 250
89 235 52 235
55 14 53 62
60 128 188 140
255 137 120 255
124 2 126 124
255 255 238 255
33 15 32 47
161 16 177 161
16 160 176 160
7 21 28 23
3 18 21 19
128 167 39 167
64 101 165 101
*/
