// Digital circuit P55.dig as structural Verilog
module P55 (
  input  clk,
  input  rst,
  input  sp_we,
  input  [7:0] sp,
  input  [7:0] limit,
  input  clear,
  output [7:0] minsp,
  output flag
);

  wire and_1_out, and_2_out, comparator_1_lt, comparator_2_lt, multiplexer_2_out, multiplexer_4_out, or_1_out;
  wire [7:0] multiplexer_1_out, multiplexer_3_out;

  or or_1 (or_1_out, rst, clear);
  Comparator #(.Bits(8)) comparator_1 (.a(sp), .b(minsp), .lt(comparator_1_lt));  // open: gt, eq
  Comparator #(.Bits(8)) comparator_2 (.a(sp), .b(limit), .lt(comparator_2_lt));  // open: gt, eq
  and and_1 (and_1_out, comparator_1_lt, sp_we);
  and and_2 (and_2_out, comparator_2_lt, sp_we);
  Multiplexer #(.Bits(8)) multiplexer_1 (.sel(and_1_out), .in_0(minsp), .in_1(sp), .out(multiplexer_1_out));
  Multiplexer #(.Bits(1)) multiplexer_2 (.sel(and_2_out), .in_0(flag), .in_1(1'b1), .out(multiplexer_2_out));
  Multiplexer #(.Bits(8)) multiplexer_3 (
    .sel(or_1_out), .in_0(multiplexer_1_out), .in_1({8{1'b1}}), .out(multiplexer_3_out));
  Multiplexer #(.Bits(1)) multiplexer_4 (
    .sel(or_1_out), .in_0(multiplexer_2_out), .in_1(1'b0), .out(multiplexer_4_out));
  D_FF #(.Bits(8)) d_ff_1 (.D(multiplexer_3_out), .C(clk), .Q(minsp));  // open: nQ
  D_FF #(.Bits(1)) d_ff_2 (.D(multiplexer_4_out), .C(clk), .Q(flag));  // open: nQ

  // Notes on the sheet:
  //   clk: Hz: 1
  //   P55 Stack guard - Digital task
  //   8-bit: a minimum register and two comparators.
  //   Allowed parts: all of the above + Add, Sub, Comparator, Neg
  //   Do not rename, move or delete the input and output pins.
endmodule

/* Test case public tests:
clk rst sp_we sp limit clear minsp flag
C 1 1 58 255 0 255 0
C 0 0 128 244 0 255 0
C 0 0 2 112 0 255 0
C 0 0 255 2 0 255 0
C 0 0 127 128 0 255 0
C 0 1 128 200 1 255 0
C 0 0 208 0 0 255 0
C 0 1 128 58 0 128 0
C 0 1 18 1 0 18 0
C 1 1 255 0 0 255 0
C 0 0 65 63 1 255 0
C 0 1 215 202 0 215 0
C 0 0 13 27 0 215 0
C 0 0 140 88 1 255 0
C 0 1 28 159 0 28 1
C 0 1 0 30 1 255 0
C 0 1 201 49 0 201 0
C 0 1 223 20 0 201 0
C 0 0 128 1 1 255 0
C 0 1 13 4 0 13 0
C 0 1 128 0 1 255 0
C 0 0 24 128 1 255 0
C 0 0 127 219 1 255 0
C 0 0 117 213 1 255 0
C 0 1 11 76 1 255 0
C 0 1 10 95 1 255 0
C 0 0 0 31 1 255 0
C 0 0 255 4 1 255 0
C 0 0 199 0 0 255 0
C 0 1 4 99 0 4 1
C 0 1 128 0 1 255 0
C 0 0 127 58 1 255 0
C 0 1 10 127 0 10 1
C 0 0 31 17 0 10 1
C 0 1 196 166 1 255 0
C 0 1 33 59 0 33 1
C 0 1 22 23 1 255 0
C 0 1 112 255 1 255 0
C 0 1 131 5 1 255 0
C 0 0 95 56 1 255 0
C 0 0 188 24 1 255 0
C 0 1 108 24 0 108 0
C 0 1 128 23 0 108 0
C 0 1 32 248 0 32 1
C 0 1 4 104 0 4 1
C 0 0 16 140 0 4 1
C 0 0 158 0 1 255 0
C 0 1 0 91 1 255 0
C 0 0 26 20 1 255 0
C 1 0 237 129 0 255 0
C 0 1 0 16 1 255 0
C 0 0 185 79 1 255 0
C 0 1 35 239 1 255 0
C 0 1 255 116 1 255 0
C 0 1 103 255 0 103 1
C 0 1 224 8 1 255 0
C 0 0 152 128 0 255 0
C 0 1 6 22 1 255 0
C 0 1 55 144 0 55 1
C 0 1 68 15 0 55 1
C 0 0 128 97 1 255 0
C 0 0 156 21 1 255 0
C 0 0 42 0 0 255 0
C 0 0 46 127 1 255 0
C 0 1 15 60 0 15 1
C 0 0 74 4 0 15 1
C 0 1 69 25 0 15 1
C 0 1 160 128 1 255 0
C 0 1 77 248 1 255 0
C 0 1 198 0 0 198 0
C 0 1 127 128 0 127 1
C 0 1 27 28 1 255 0
C 0 1 48 128 0 48 1
C 0 1 2 0 0 2 1
C 0 0 128 131 1 255 0
C 1 1 144 112 1 255 0
C 0 0 141 1 1 255 0
C 0 1 41 209 0 41 1
C 0 0 10 127 0 41 1
C 0 0 127 223 1 255 0
C 0 1 167 249 0 167 1
C 0 1 200 92 0 167 1
C 0 0 10 162 0 167 1
C 0 1 30 20 0 30 1
C 0 1 231 104 0 30 1
C 0 1 120 45 0 30 1
C 0 0 13 127 0 30 1
C 0 1 46 0 1 255 0
C 0 0 128 128 0 255 0
C 0 1 195 255 0 195 1
C 0 1 81 30 0 81 1
C 0 1 91 25 1 255 0
C 0 1 28 82 1 255 0
C 1 1 174 62 1 255 0
C 0 0 255 39 1 255 0
C 0 0 73 85 0 255 0
C 0 0 0 127 1 255 0
C 0 0 36 127 1 255 0
C 0 0 20 94 0 255 0
C 0 0 128 0 1 255 0
C 0 1 127 42 1 255 0
C 0 0 0 39 0 255 0
C 0 0 68 5 1 255 0
C 0 1 14 127 0 14 1
C 0 1 255 128 1 255 0
C 0 0 228 248 1 255 0
C 0 1 158 255 0 158 1
C 0 0 128 30 1 255 0
C 0 1 189 3 0 189 0
C 0 1 76 127 1 255 0
C 0 0 8 4 0 255 0
C 0 1 144 0 0 144 0
C 0 1 146 255 0 144 1
C 1 0 106 68 0 255 0
C 0 0 255 127 0 255 0
C 0 1 2 1 0 2 0
C 0 0 70 56 0 2 0
C 0 1 128 56 1 255 0
C 0 1 255 147 0 255 0
C 0 0 40 237 0 255 0
C 0 0 128 15 0 255 0
C 0 0 145 12 0 255 0
C 1 1 201 101 1 255 0
C 0 1 11 115 0 11 1
C 0 0 50 203 1 255 0
C 0 0 158 202 1 255 0
C 0 1 5 18 0 5 1
C 0 0 1 26 1 255 0
C 0 0 239 255 1 255 0
C 0 1 231 168 0 231 0
C 0 0 25 86 1 255 0
C 0 0 36 1 0 255 0
C 0 0 221 104 1 255 0
C 0 0 26 184 0 255 0
C 0 1 227 140 0 227 0
C 0 0 19 203 0 227 0
C 0 1 13 237 0 13 1
C 0 0 26 8 1 255 0
C 0 0 127 26 0 255 0
C 0 1 170 26 1 255 0
C 0 0 128 24 1 255 0
C 0 0 7 40 0 255 0
C 0 1 98 29 1 255 0
C 0 1 27 125 1 255 0
C 0 1 31 0 0 31 0
C 0 1 10 36 1 255 0
C 0 1 218 135 0 218 0
C 0 1 3 26 1 255 0
C 0 0 128 171 0 255 0
C 0 0 18 127 1 255 0
C 0 1 64 143 1 255 0
C 0 0 233 0 0 255 0
C 0 1 24 112 1 255 0
C 0 1 15 6 0 15 0
C 0 1 130 99 1 255 0
C 0 0 192 0 0 255 0
C 0 1 14 9 1 255 0
C 0 1 159 128 1 255 0
C 0 0 40 21 0 255 0
C 0 1 0 128 0 0 1
*/
